# Fritzing sketch eqtiny (saved by Fritzing 0.9.3b)
circuit board: 8.46667cm x 5.64444cm
breadboards: 1

parts:
  U1 = attiny85 [package=dip]
  msgeq7 = IC, DIP package, 8 pins [chip_label=msgeq7]
  R1 = Resistor [tolerance=±5% resistance=10k package=THT]
  Part1 = Breakout Board for Electret Microphone
  C1 = Ceramic Capacitor [capacitance=33pF package="100 mil [THT, multilayer]"]
  R2 = Resistor [tolerance=±5% resistance=200k package=THT]
  C2 = Ceramic Capacitor [capacitance=0.1µF package="100 mil [THT, multilayer]"]
  C3 = Ceramic Capacitor [capacitance=0.1µF package="100 mil [THT, multilayer]"]
  R3 = Resistor [tolerance=±5% resistance=22k package=THT]
  C4 = Ceramic Capacitor [capacitance=0.01µF package="100 mil [THT, multilayer]"]

nets:
  N1: U1.Pin_1, R1.Pin_1
  N2: U1.Pin_2, msgeq7.pin3
  N3: U1.Pin_3, msgeq7.pin4
  N4: U1.Pin_4, msgeq7.pin2, Part1.GND, C1.1, C2.0, C3.0
  N5: U1.Pin_7, msgeq7.pin7
  N6: U1.Pin_8, msgeq7.pin1, R1.Pin_0, Part1.VCC, R2.Pin_1, C3.1
  N7: msgeq7.pin5, C4.0
  N8: msgeq7.pin6, C2.1
  N9: msgeq7.pin8, C1.0, R2.Pin_0
  N10: Part1.AUD, R3.Pin_1
  N11: R3.Pin_0, C4.1

custom parts:
  Breakout Board for Electret Microphone: Description: Ready to add audio to your next project? This small breakout board couples a small electret microphone with a 100x opamp to amplify the sounds of voice, door knocks, etc loud enough to be picked up by a microcontroller's Analog to Digital converter. Unit comes fully assembled as shown. Works from 2.7V up to 5.5V. Documents: Schematic Example PIC ADC Code OPA344 Datasheet Example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
